// Logisim project FPA.circ as structural Verilog: 4 circuits, main circuit main
module main (
  input  [31:0] Input1,
  input  [31:0] Input2,
  output INF,
  output NaN1,
  output Denormalized1,
  output Nan2,
  output Denormalized2,
  output [31:0] out_8,
  output [31:0] fraction_result,
  output Denorm,
  output mainOverflow,
  output out_12,
  output [31:0] larger_fraction,
  output [8:0] out_14,
  output mainUnderflow,
  output out_16,
  output [31:0] smaller_fraction,
  output [8:0] out_18,
  output NAN,
  output output_sign,
  output [31:0] Output,
  output [31:0] Output_final
);

  wire and_1_out, main_4_excdenorm, main_4_overflow, main_4_underflow, main_5_denormalized_input1,
       main_5_nan_input1, multiplexer_1_out, n1checker_1_check_1_bit, not_1_out, xor_1_out;
  wire [8:0] maincomparator_1_larger_2;
  wire [31:0] fractionextender_1_out_2, fractionextender_2_out_2, main_1_valid_fraction1,
       main_1_valid_fraction2, main_2_fraction_result, rounder_out_2;

  fractionExtender fractionextender_1 (.in_1(Input1[21:0]), .out_2(fractionextender_1_out_2));
  fractionExtender fractionextender_2 (.in_1(Input2[21:0]), .out_2(fractionextender_2_out_2));
  input_validator_main main_1 (
    .exp1(Input1[30:22]), .frac1(fractionextender_1_out_2), .exp2(Input2[30:22]),
    .frac2(fractionextender_2_out_2), .NaN_input1(NaN1), .Denormalized_input1(Denormalized1),
    .Valid_Fraction1(main_1_valid_fraction1), .Nan_input2(Nan2), .denormalized_input2(Denormalized2),
    .valid_fraction2(main_1_valid_fraction2));
  mainComparator maincomparator_1 (
    .Input1(main_1_valid_fraction1), .Input2(main_1_valid_fraction2), .X(Input1[30:22]), .Y(Input2[30:22]),
    .signX(Input1[31]), .signY(Input2[31]), .larger(larger_fraction), .samller(smaller_fraction),
    .LARGER_2(maincomparator_1_larger_2), .outputSign(Output[31]));  // open: largerByExponent, smallerByExponent, largerByFraction, smallerByFraction, SMALLER, X_Y, DIFFERENCE, largerSignByExponent, largerSign, smallerSignByExponent, smallerSign, largerSignByFraction, smallerSignByFraction
  adder_subtractor_main main_2 (
    .frac1(larger_fraction), .frac2(smaller_fraction), .sign1(Input1[31]), .sign2(Input2[31]),
    .fraction_result(main_2_fraction_result));
  Normalizer_main main_3 (
    .fraction(main_2_fraction_result), .exponent(maincomparator_1_larger_2),
    .normalized_fraction(fraction_result), .Underflow(out_12), .Overflow(out_16), .finalExponent(out_18));  // open: excDenorm, INF
  xor xor_1 (xor_1_out, out_16, out_12);
  Normalizer_main main_4 (
    .fraction(rounder_out_2), .exponent(out_18), .excDenorm(main_4_excdenorm), .INF(INF),
    .normalized_fraction(out_8), .Underflow(main_4_underflow), .Overflow(main_4_overflow),
    .finalExponent(out_14));
  Rounder_main rounder (.result(fraction_result), .out_2(rounder_out_2));
  _1checker u_1checker_1 (.in_1(out_8), .check_1_bit(n1checker_1_check_1_bit));
  Multiplexer multiplexer_1 (
    .in0(main_4_underflow), .in1(out_12), .out(multiplexer_1_out), .sel(xor_1_out));  // open: en
  Multiplexer multiplexer_2 (.in0(main_4_overflow), .in1(out_16), .out(mainOverflow), .sel(xor_1_out));  // open: en
  Multiplexer #(.width(32)) multiplexer_3 (
    .in0({32{1'b0}}), .in1({Output[31], out_14, out_8[29:8]}), .out(Output_final),
    .sel(n1checker_1_check_1_bit));  // open: en
  input_validator_main main_5 (
    .exp1(out_14), .frac1({Output[31], out_14, out_8[29:8]}), .NaN_input1(main_5_nan_input1),
    .Denormalized_input1(main_5_denormalized_input1));  // open: exp2, frac2, Valid_Fraction1, Nan_input2, denormalized_input2, valid_fraction2
  or or_1 (Denorm, main_4_excdenorm, main_5_denormalized_input1);
  not not_1 (not_1_out, Denorm);
  and and_1 (and_1_out, main_5_nan_input1, mainOverflow);
  and and_2 (mainUnderflow, not_1_out, multiplexer_1_out);
  or or_2 (NAN, and_1_out, NaN1, Nan2);

  assign Output[30:0] = {out_14, out_8[29:8]};
  assign output_sign = Output[31];
endmodule

// extender
module fractionExtender (
  input  [21:0] in_1,
  output [31:0] out_2
);


  assign out_2 = {2'b01, in_1, {8{1'b0}}};
endmodule

module FPA (
  input  [31:0] INPUT,
  input  [31:0] INPUT2,
  output DENORM,
  output INF,
  output OVERFLOW,
  output UNDERFLOW,
  output NAN,
  output [31:0] OUTPUT
);

  wire main_1_denorm, main_1_denormalized1, main_1_denormalized2, or_1_out;

  main main_1 (
    .Input1(INPUT), .Input2(INPUT2), .INF(INF), .Denormalized1(main_1_denormalized1),
    .Denormalized2(main_1_denormalized2), .Denorm(main_1_denorm), .mainOverflow(OVERFLOW),
    .mainUnderflow(UNDERFLOW), .NAN(NAN), .Output_final(OUTPUT));  // open: NaN1, Nan2, out_8, fraction_result, out_12, larger_fraction, out_14, out_16, smaller_fraction, out_18, output_sign, Output
  or or_1 (or_1_out, main_1_denorm, main_1_denormalized2);
  or or_2 (DENORM, or_1_out, main_1_denormalized1);
endmodule

module MAIN_FPA (
  input  [31:0] INPUT1,
  input  [31:0] INPUT2,
  output DENOMAL,
  output INF,
  output OVERFLOW,
  output UNDERFLOW,
  output NaN,
  output [31:0] OUTPUT
);

  FPA fpa_1 (
    .INPUT(INPUT1), .INPUT2(INPUT2), .DENORM(DENOMAL), .INF(INF), .OVERFLOW(OVERFLOW), .UNDERFLOW(UNDERFLOW),
    .NAN(NaN), .OUTPUT(OUTPUT));

  // Notes on the sheet:
  //   MAIN FPA CIRCUIT
endmodule
