// Logisim project Normalizer.circ as structural Verilog: 2 circuits, main circuit main
module main (
  input  [31:0] fraction,
  input  [8:0] exponent,
  output excDenorm,
  output INF,
  output [31:0] normalized_fraction,
  output Underflow,
  output Overflow,
  output [8:0] finalExponent
);

  wire alu_12_bit_1_p5, alu_12_bit_1_p6, and_3_out, comparator_1_eq, comparator_1_gt,
       n1checker_1_check_1_bit, n1checker_2_check_1_bit, nor_1_out, not_2_out, not_3_out, not_4_out,
       not_5_out, or_1_out, or_2_out, or_3_out, or_4_out, or_5_out, or_6_out, or_7_out, or_8_out, or_9_out;
  wire [0:0] not_1_out;
  wire [1:0] alu_12_bit_1_p4_2;
  wire [4:0] n7408_2_p3, priority_encoder_1_out;
  wire [7:0] alu_8_bit_1_p4;
  wire [9:9] alu_12_bit_1_p4;
  wire [11:0] multiplexer_1_out;
  wire [31:0] shifter_1_out, shifter_2_out;

  or or_1 (or_1_out, exponent[8], exponent[7], exponent[6], exponent[5]);
  nor nor_1 (nor_1_out, fraction[31], fraction[30]);
  or or_2 (or_2_out, exponent[4], exponent[3], exponent[2], exponent[1], exponent[0]);
  Shifter #(.width(32), .shift("lr")) shifter_1 (.in(fraction), .\dist (5'b00001), .out(shifter_1_out));
  Priority_Encoder #(.select(5)) priority_encoder_1 (
    .in0(1'b1), .in1(1'b0), .in2(fraction[0]), .in3(fraction[1]), .in4(fraction[2]), .in5(fraction[3]),
    .in6(fraction[4]), .in7(fraction[5]), .in8(fraction[6]), .in9(fraction[7]), .in10(fraction[8]),
    .in11(fraction[9]), .in12(fraction[10]), .in13(fraction[11]), .in14(fraction[12]), .in15(fraction[13]),
    .in16(fraction[14]), .in17(fraction[15]), .in18(fraction[16]), .in19(fraction[17]), .in20(fraction[18]),
    .in21(fraction[19]), .in22(fraction[20]), .in23(fraction[21]), .in24(fraction[22]), .in25(fraction[23]),
    .in26(fraction[24]), .in27(fraction[25]), .in28(fraction[26]), .in29(fraction[27]), .in30(fraction[28]),
    .in31(fraction[29]), .out(priority_encoder_1_out));  // open: gs, en_out, en_in
  or or_3 (or_3_out, or_2_out, or_1_out);
  // ALU_8_bit alu_8_bit_1: pin names not known; wires that end beside it: 8'h20, {3'b000, priority_encoder_1_out}, 2'b11, alu_8_bit_1_p4
  _1checker u_1checker_1 (.in_1(fraction), .check_1_bit(n1checker_1_check_1_bit));
  // _7408 7408_1: pin names not known; wires that end beside it: nor_1_out, alu_8_bit_1_p4[4], n7408_2_p3[4], nor_1_out, alu_8_bit_1_p4[3], n7408_2_p3[3], 1'b0, 1'b1, alu_8_bit_1_p4[2], nor_1_out, n7408_2_p3[2], nor_1_out, alu_8_bit_1_p4[1], n7408_2_p3[1]
  Multiplexer #(.width(12)) multiplexer_1 (
    .in0({{7{1'b0}}, n7408_2_p3}), .in1(12'h1), .out(multiplexer_1_out), .sel(fraction[31]));  // open: en
  Shifter #(.width(32)) shifter_2 (.in(fraction), .\dist (n7408_2_p3), .out(shifter_2_out));
  not not_1 (not_1_out[0], fraction[31]);
  // _7408 7408_2: pin names not known; wires that end beside it: alu_8_bit_1_p4[0], nor_1_out, n7408_2_p3[0], 1'b0, 1'b1
  Multiplexer #(.width(32)) multiplexer_2 (
    .in0(shifter_2_out), .in1(shifter_1_out), .out(normalized_fraction), .sel(fraction[31]));  // open: en
  // ALU_12_bit alu_12_bit_1: pin names not known; wires that end beside it: {3'b000, exponent}, multiplexer_1_out, {1'b1, not_1_out[0]}, {alu_12_bit_1_p4_2, alu_12_bit_1_p4[9], finalExponent}, alu_12_bit_1_p5, alu_12_bit_1_p6
  or or_4 (or_4_out, n1checker_1_check_1_bit, or_3_out);
  or or_5 (or_5_out, alu_12_bit_1_p5, alu_12_bit_1_p6);
  Comparator #(.width(10), .mode("unsigned")) comparator_1 (
    .a({alu_12_bit_1_p4[9], finalExponent}), .b(10'h1ff), .gt(comparator_1_gt), .eq(comparator_1_eq));  // open: lt
  not not_2 (not_2_out, n1checker_1_check_1_bit);
  and and_1 (Underflow, or_5_out, or_4_out);
  not not_3 (not_3_out, alu_12_bit_1_p6);
  or or_6 (or_6_out, finalExponent[8], finalExponent[7], finalExponent[6], finalExponent[5]);
  or or_7 (or_7_out, comparator_1_gt, comparator_1_eq);
  or or_8 (or_8_out, finalExponent[4], finalExponent[3], finalExponent[2], finalExponent[1], finalExponent[0]);
  and and_2 (INF, not_2_out, comparator_1_eq);
  _1checker u_1checker_2 (.in_1(normalized_fraction), .check_1_bit(n1checker_2_check_1_bit));
  not not_4 (not_4_out, INF);
  and and_3 (and_3_out, or_7_out, not_3_out);
  and and_4 (Overflow, and_3_out, not_4_out);
  or or_9 (or_9_out, or_8_out, or_6_out);
  not not_5 (not_5_out, or_9_out);
  and and_5 (excDenorm, n1checker_2_check_1_bit, not_5_out);

  // Notes on the sheet:
  //   right shifting case
  //   left shift?
  //   12 bit exponent
  //   left shifted
  //   right shifted
  //   left shifting case
  //   shift for exponent
endmodule

module _1checker (
  input  [31:0] in_1,
  output check_1_bit
);

  wire n7432_1_p3, n7432_1_p6, n7432_1_p10, n7432_1_p11, n7432_2_p3, n7432_2_p6, n7432_2_p10, n7432_2_p11,
       n7432_3_p3, n7432_3_p6, n7432_3_p10, n7432_3_p11, n7432_4_p3, n7432_4_p6, n7432_4_p10, n7432_4_p11,
       n7432_5_p1, n7432_5_p3, n7432_5_p6, n7432_6_p3, n7432_6_p6, n7432_6_p10, n7432_6_p11, n7432_7_p3,
       n7432_7_p6, n7432_7_p10, n7432_7_p11, n7432_8_p3, n7432_8_p6, n7432_8_p10;

  // _7432 7432_1: pin names not known; wires that end beside it: in_1[0], in_1[1], n7432_1_p3, n7432_1_p3, in_1[2], n7432_1_p6, 1'b0, 1'b1, in_1[4], n7432_1_p10, n7432_1_p11, in_1[3], n7432_1_p6, n7432_1_p10
  // _7432 7432_2: pin names not known; wires that end beside it: n7432_1_p11, in_1[5], n7432_2_p3, n7432_2_p3, in_1[6], n7432_2_p6, 1'b0, 1'b1, in_1[8], n7432_2_p10, n7432_2_p11, in_1[7], n7432_2_p6, n7432_2_p10
  // _7432 7432_3: pin names not known; wires that end beside it: n7432_2_p11, in_1[9], n7432_3_p3, n7432_3_p3, in_1[10], n7432_3_p6, 1'b0, 1'b1, in_1[12], n7432_3_p10, n7432_3_p11, in_1[11], n7432_3_p6, n7432_3_p10
  // _7432 7432_4: pin names not known; wires that end beside it: n7432_3_p11, in_1[13], n7432_4_p3, n7432_4_p3, in_1[14], n7432_4_p6, 1'b0, 1'b1, in_1[16], n7432_4_p10, n7432_4_p11, in_1[15], n7432_4_p6, n7432_4_p10
  // _7432 7432_5: pin names not known; wires that end beside it: n7432_5_p1, in_1[29], n7432_5_p3, n7432_5_p3, in_1[30], n7432_5_p6, 1'b0, 1'b1, in_1[31], n7432_5_p6, check_1_bit
  // _7432 7432_6: pin names not known; wires that end beside it: n7432_4_p11, in_1[17], n7432_6_p3, n7432_6_p3, in_1[18], n7432_6_p6, 1'b0, 1'b1, in_1[20], n7432_6_p10, n7432_6_p11, in_1[19], n7432_6_p6, n7432_6_p10
  // _7432 7432_7: pin names not known; wires that end beside it: n7432_6_p11, in_1[21], n7432_7_p3, n7432_7_p3, in_1[22], n7432_7_p6, 1'b0, 1'b1, in_1[24], n7432_7_p10, n7432_7_p11, in_1[23], n7432_7_p6, n7432_7_p10
  // _7432 7432_8: pin names not known; wires that end beside it: n7432_7_p11, in_1[25], n7432_8_p3, n7432_8_p3, in_1[26], n7432_8_p6, 1'b0, 1'b1, in_1[28], n7432_8_p10, n7432_5_p1, in_1[27], n7432_8_p6, n7432_8_p10
endmodule
