// Logisim project Rounder.circ as structural Verilog: 1 circuit, main circuit main
module main (
  input  [31:0] result,
  output [31:0] out_2
);

  wire and_1_out, and_2_out, or_1_out, or_2_out;
  wire [23:0] adder_1_out;

  or or_1 (or_1_out, result[6], result[5]);
  Adder #(.width(24)) adder_1 (.a(result[31:8]), .b(24'h1), .out(adder_1_out));  // open: cin, cout
  and and_1 (and_1_out, result[7], or_1_out);
  and and_2 (and_2_out, result[7], result[8]);
  or or_2 (or_2_out, and_1_out, and_2_out);
  Multiplexer #(.width(24)) multiplexer_1 (
    .in0(result[31:8]), .in1(adder_1_out), .out(out_2[31:8]), .sel(or_2_out));  // open: en

  assign out_2[7:0] = {8{1'b0}};

  // Notes on the sheet:
  //   G-1,G,R,S
  //   G(R+S)
endmodule
