// Logisim project adder_subtractor.circ as structural Verilog: 1 circuit, main circuit main
module main (
  input  [31:0] frac1,
  input  [31:0] frac2,
  input  sign1,
  input  sign2,
  output [31:0] fraction_result
);

  wire alu_32_bit_1_p5, alu_32_bit_1_p6;
  wire [0:0] xor_1_out;
  wire [1:1] n7408_1_p3;

  xor xor_1 (xor_1_out[0], sign1, sign2);
  // ALU_32_bit alu_32_bit_1: pin names not known; wires that end beside it: sign1, frac1, frac2, {1'b1, xor_1_out[0]}, alu_32_bit_1_p5, alu_32_bit_1_p6
  // _7408 7408_1: pin names not known; wires that end beside it: alu_32_bit_1_p6, xor_1_out[0], n7408_1_p3[1], 1'b0, 1'b1
  // ALU_32_bit alu_32_bit_2: pin names not known; wires that end beside it: alu_32_bit_1_p5, {32{1'b0}}, {n7408_1_p3[1], 1'b0}, fraction_result
endmodule
