// Logisim project check_single_input_flags.circ as structural Verilog: 1 circuit, main circuit main
module main (
  input  exp_all_1,
  input  frac_1,
  input  exp_1,
  output NaN,
  output Denormalized_flag
);

  wire not_1_out;

  not not_1 (not_1_out, exp_1);
  and and_1 (NaN, exp_all_1, frac_1);
  and and_2 (Denormalized_flag, frac_1, not_1_out);
endmodule
