// Logisim project compareBits.circ as structural Verilog: 2 circuits, main circuit mainComparator
// Alu16
module Alu_16 (
  input  [15:0] Input_1,
  input  [15:0] Input_2,
  input  [1:0] Control,
  output [8:0] out_4,
  output carry,
  output Z_flag,
  output sign
);

  wire adder_1_cout, bitfinder_1_found, subtractor_1_bout;
  wire [15:0] adder_1_out, negator_1_out, subtractor_1_out;
  wire [15:10] multiplexer_1_out;

  Negator #(.width(16)) negator_1 (.in(Input_1), .out(negator_1_out));
  Adder #(.width(16)) adder_1 (.a(Input_1), .b(Input_2), .out(adder_1_out), .cin(1'b0), .cout(adder_1_cout));
  Subtractor #(.width(16)) subtractor_1 (
    .a(Input_1), .b(Input_2), .out(subtractor_1_out), .bin(1'b0), .bout(subtractor_1_bout));
  Multiplexer #(.select(2), .width(16)) multiplexer_1 (
    .in0(Input_1), .in1(negator_1_out), .in2(adder_1_out), .in3(subtractor_1_out),
    .out({multiplexer_1_out, sign, out_4}), .sel(Control), .en(1'b1));
  Multiplexer #(.select(2)) multiplexer_2 (
    .in0(1'b0), .in1(1'b0), .in2(adder_1_cout), .in3(subtractor_1_bout), .out(carry), .sel(Control), .en(1'b1));
  BitFinder #(.width(16)) bitfinder_1 (
    .in({multiplexer_1_out, sign, out_4}), .found(bitfinder_1_found));  // open: index
  not not_1 (Z_flag, bitfinder_1_found);
endmodule

module mainComparator (
  input  [31:0] Input1,
  input  [31:0] Input2,
  input  [8:0] X,
  input  [8:0] Y,
  input  signX,
  input  signY,
  output [31:0] larger,
  output [31:0] largerByExponent,
  output [31:0] smallerByExponent,
  output [31:0] samller,
  output [31:0] largerByFraction,
  output [31:0] smallerByFraction,
  output [8:0] SMALLER,
  output X_Y,
  output [8:0] LARGER_2,
  output [4:0] DIFFERENCE,
  output largerSignByExponent,
  output outputSign,
  output largerSign,
  output smallerSignByExponent,
  output smallerSign,
  output largerSignByFraction,
  output smallerSignByFraction
);

  wire alu_16_1_z_flag, alu_16_3_sign, and_1_out, and_2_out, comparator_1_eq, comparator_1_gt, or_1_out,
       or_2_out, or_3_out;
  wire [8:0] alu_16_1_out_4, alu_16_2_out_4;
  wire [15:5] multiplexer_15_out;
  wire [31:0] multiplexer_12_out, shifter_1_out, undriven;

  Comparator #(.width(32), .mode("unsigned")) comparator_1 (
    .a(Input1), .b(Input2), .gt(comparator_1_gt), .eq(comparator_1_eq));  // open: lt
  Alu_16 alu_16_1 (
    .Input_1({{7{1'b0}}, X}), .Input_2({{7{1'b0}}, Y}), .Control(2'b11), .out_4(alu_16_1_out_4),
    .Z_flag(alu_16_1_z_flag), .sign(X_Y));  // open: carry
  Multiplexer #(.width(32)) multiplexer_1 (.in0(Input1), .in1(Input2), .out(largerByExponent), .sel(X_Y));  // open: en
  Multiplexer #(.width(32)) multiplexer_2 (.in0(Input2), .in1(Input1), .out(smallerByExponent), .sel(X_Y));  // open: en
  Multiplexer #(.width(32)) multiplexer_3 (
    .in0(Input2), .in1(Input1), .out(largerByFraction), .sel(comparator_1_gt));  // open: en
  Multiplexer #(.width(32)) multiplexer_4 (
    .in0(Input1), .in1(Input2), .out(smallerByFraction), .sel(comparator_1_gt));  // open: en
  Multiplexer #(.width(9)) multiplexer_5 (.in0(Y), .in1(X), .out(SMALLER), .sel(X_Y), .en(1'b1));
  Multiplexer #(.width(9)) multiplexer_6 (.in0(X), .in1(Y), .out(LARGER_2), .sel(X_Y), .en(1'b1));
  Multiplexer multiplexer_7 (.in0(signX), .in1(signY), .out(largerSignByExponent), .sel(X_Y));  // open: en
  Multiplexer multiplexer_8 (.in0(signY), .in1(signX), .out(smallerSignByExponent), .sel(X_Y));  // open: en
  Multiplexer multiplexer_9 (.in0(signY), .in1(signX), .out(largerSignByFraction), .sel(comparator_1_gt));  // open: en
  Multiplexer multiplexer_10 (
    .in0(signX), .in1(signY), .out(smallerSignByFraction), .sel(comparator_1_gt));  // open: en
  and and_1 (and_1_out, signX, signY);
  Alu_16 alu_16_2 (
    .Input_1({{7{1'b0}}, alu_16_1_out_4}), .Input_2({16{1'b0}}), .Control({1'b0, X_Y}), .out_4(alu_16_2_out_4));  // open: carry, Z_flag, sign
  Multiplexer #(.width(32)) multiplexer_11 (
    .in0(largerByExponent), .in1(largerByFraction), .out(larger), .sel(alu_16_1_z_flag));  // open: en
  Multiplexer #(.width(32)) multiplexer_12 (
    .in0(smallerByExponent), .in1(smallerByFraction), .out(multiplexer_12_out), .sel(alu_16_1_z_flag));  // open: en
  Multiplexer multiplexer_13 (
    .in0(largerSignByExponent), .in1(largerSignByFraction), .out(largerSign), .sel(alu_16_1_z_flag));  // open: en
  Multiplexer multiplexer_14 (
    .in0(smallerSignByExponent), .in1(smallerSignByFraction), .out(smallerSign), .sel(alu_16_1_z_flag));  // open: en
  and and_2 (and_2_out, comparator_1_eq, alu_16_1_z_flag);
  Alu_16 alu_16_3 (
    .Input_1({{7{1'b0}}, alu_16_2_out_4}), .Input_2(16'h1f), .Control(2'b11), .sign(alu_16_3_sign));  // open: out_4, carry, Z_flag
  Multiplexer #(.width(16)) multiplexer_15 (
    .in0(16'h1f), .in1({{7{1'b0}}, alu_16_2_out_4}), .out({multiplexer_15_out, DIFFERENCE}),
    .sel(alu_16_3_sign), .en(1'b1));
  Multiplexer multiplexer_16 (.in0(largerSign), .in1(and_1_out), .out(outputSign), .sel(and_2_out));  // open: en
  or or_1 (or_1_out, multiplexer_15_out[14], multiplexer_15_out[13], multiplexer_15_out[12], multiplexer_15_out[11], multiplexer_15_out[10]);
  or or_2 (or_2_out, multiplexer_15_out[15], or_1_out, or_3_out);
  Shifter #(.width(32), .shift("lr")) shifter_1 (.in(multiplexer_12_out), .\dist (DIFFERENCE), .out(shifter_1_out));
  or or_3 (or_3_out, multiplexer_15_out[9], multiplexer_15_out[8], multiplexer_15_out[7], multiplexer_15_out[6], multiplexer_15_out[5]);
  Multiplexer #(.width(32)) multiplexer_17 (
    .in0(shifter_1_out), .in1(undriven), .out(samller), .sel(or_2_out));  // open: en

  // Notes on the sheet:
  //   larger
endmodule
