// Logisim project input_validator.circ as structural Verilog: 1 circuit, main circuit main
module main (
  input  [8:0] exp1,
  input  [31:0] frac1,
  input  [8:0] exp2,
  input  [31:0] frac2,
  output NaN_input1,
  output Denormalized_input1,
  output [31:0] Valid_Fraction1,
  output Nan_input2,
  output denormalized_input2,
  output [31:0] valid_fraction2
);

  wire input1_check_exponent_all_1, input1_check_exponent_contains_1, input1_check_fraction_contains_1,
       Input2_check_exponent_all_1, Input2_check_exponent_contains_1, Input2_check_fraction_contains_1;

  single_input_check_main input1 (
    .exponent(exp1), .fraction(frac1), .check_exponent_all_1(input1_check_exponent_all_1),
    .check_exponent_contains_1(input1_check_exponent_contains_1), .fraction_2(Valid_Fraction1),
    .check_fraction_contains_1(input1_check_fraction_contains_1));
  single_input_check_main Input2 (
    .exponent(exp2), .fraction(frac2), .check_exponent_all_1(Input2_check_exponent_all_1),
    .check_exponent_contains_1(Input2_check_exponent_contains_1), .fraction_2(valid_fraction2),
    .check_fraction_contains_1(Input2_check_fraction_contains_1));
  check_single_input_flags_main main_1 (
    .exp_all_1(input1_check_exponent_all_1), .frac_1(input1_check_fraction_contains_1),
    .exp_1(input1_check_exponent_contains_1), .NaN(NaN_input1), .Denormalized_flag(Denormalized_input1));
  check_single_input_flags_main main_2 (
    .exp_all_1(Input2_check_exponent_all_1), .frac_1(Input2_check_fraction_contains_1),
    .exp_1(Input2_check_exponent_contains_1), .NaN(Nan_input2), .Denormalized_flag(denormalized_input2));
endmodule
